# Fritzing sketch midi_controller_pico (saved by Fritzing 1.0.4)

parts:
  Pico/Pico2_Mod_1 = Raspberry Pi Pico or Pico 2
  S1 = Round Pushbutton
  S2 = Round Pushbutton
  S3 = Round Pushbutton
  S4 = Round Pushbutton
  S5 = Round Pushbutton
  Part1 = Adafruit 4-channel I2C-safe Bi-directional Logic Level Converter [part_number="Adafruit #757"]
  Grove1 = TM1637 7segment 4digit display
  R1 = Resistor [tolerance=±5% resistance=220 package="2010 [SMD]"]
  R2 = Resistor [tolerance=±5% resistance=220 package="2010 [SMD]"]
  R3 = Resistor [tolerance=±5% resistance=220 package="2010 [SMD]"]
  LED1 = LED - 3mm [color="Blue (430nm)" current=0.030A package="3 mm [THT]"]
  LED2 = LED - 3mm [color="Blue (430nm)" current=0.030A package="3 mm [THT]"]
  LED3 = LED - 3mm [color="Blue (430nm)" current=0.030A package="3 mm [THT]"]
  R4 = Resistor [tolerance=±5% resistance=220 package="2010 [SMD]"]
  DIN1 = DIN-5 jack (MIDI) [package=THT]
  LED4 = LED - 3mm [color="Blue (430nm)" current=0.030A package="3 mm [THT]"]
  R5 = Resistor [tolerance=±5% resistance=220 package="2010 [SMD]"]
  J1 = Power Jack [package=power_jack_smd]
  S6 = Pushbutton [package="[THT]"]

nets:
  N1: Pico/Pico2_Mod_1.pin_1, Part1.LV
  GND: Pico/Pico2_Mod_1.pin_3, Pico/Pico2_Mod_1.pin_13, Pico/Pico2_Mod_1.pin_18, Pico/Pico2_Mod_1.pin_23, Pico/Pico2_Mod_1.pin_33, Pico/Pico2_Mod_1.pin_38, S1.leg0, S2.leg0, S3.leg0, S4.leg0, S5.leg0, Part1.GND, Grove1.GND, LED1.cathode, LED2.cathode, LED3.cathode, DIN1.2, LED4.cathode, J1.GND, S6.Pin_1, S6.Pin_2
  N2: Pico/Pico2_Mod_1.pin_9, S1.leg1
  N3: Pico/Pico2_Mod_1.pin_10, S2.leg1
  N4: Pico/Pico2_Mod_1.pin_11, S3.leg1
  N5: Pico/Pico2_Mod_1.pin_12, S4.leg1
  N6: Pico/Pico2_Mod_1.pin_14, S5.leg1
  N7: Pico/Pico2_Mod_1.pin_15, S6.Pin_3, S6.Pin_4
  N8: Pico/Pico2_Mod_1.pin_24, R1.Pin_1
  N9: Pico/Pico2_Mod_1.pin_25, R2.Pin_1
  N10: Pico/Pico2_Mod_1.pin_26, R3.Pin_1
  N11: Pico/Pico2_Mod_1.pin_27, R5.Pin_1
  N12: Pico/Pico2_Mod_1.pin_31, Grove1.CLK
  N13: Pico/Pico2_Mod_1.pin_32, Grove1.DIO
  N14: Pico/Pico2_Mod_1.pin_36, Grove1.Vcc
  N15: Pico/Pico2_Mod_1.pin_39, J1.PWR
  N16: Pico/Pico2_Mod_1.pin_40, R4.Pin_0
  N17: Part1.HV, DIN1.5
  N18: R1.Pin_0, LED1.anode
  N19: R2.Pin_0, LED2.anode
  N20: R3.Pin_0, LED3.anode
  N21: R4.Pin_1, DIN1.4
  N22: LED4.anode, R5.Pin_0

custom parts:
  Raspberry Pi Pico or Pico 2: Raspberry Pi Pico and Pico 2. Based around the RP2040 and RP2350 microcontrollers respectively, Picos are low cost microcontroller device bringing Raspberry Pi quality, cost, and easy of use to the microcontroller space. Jan 2021, Split part in to two versions: tht (this one) and SMD. This one will drill holes for a .1 in header in pcb to allow plugging in the module as well as providing pads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
  Adafruit 4-channel I2C-safe Bi-directional Logic Level Converter: Because the Arduino (and Basic Stamp) are 5V devices, and most modern sensors, displays, flash cards and modes are 3.3V-only, many makers find that they need to perform level shifting/conversion to protect the 3.3V device from 5V. We do have some other handy level shifters in the shop, from the DIP 74LVC245 to the fancy bi-directional TXB0108. However, neither of these are happy to work with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
